# Fritzing sketch Untitled Sketch (saved by Fritzing 0.8.5b)
breadboards: 1

parts:
  Componente1 = SRF05 Ultrasonic Rangefinder
  Componente2 = Arduino Uno (Rev3)
  LED1 = LED - 5mm [color="Red (633nm)" package="5 mm [THT]"]
  LED2 = LED - 5mm [color="Red (633nm)" package="5 mm [THT]"]
  R1 = Resistor [tolerance=±5% resistance=220 package=THT]
  R2 = Resistor [tolerance=±5% resistance=220 package=THT]
  DHT1 = DHT11 Humitidy and Temperature Sensor
  R3 = Resistor [package="2512 [SMD]"]

nets:
  VCC: Componente1.VCC, DHT1.VDD, R3.Pin_1
  N1: Componente1.Trig, Componente2.D12/MISO
  N2: Componente1.Echo, Componente2.D13/SCK
  GND: Componente1.GND, LED1.anode, LED2.anode, DHT1.GND
  N3: Componente2.D6_PWM, R2.Pin_0
  N4: Componente2.D7, R1.Pin_0
  N5: LED1.cathode, R2.Pin_1
  N6: LED2.cathode, R1.Pin_1
  N7: DHT1.DATA, R3.Pin_0

notes:
  I2C
  SCL- A5
  SDA- A4

custom parts:
  DHT11 Humitidy and Temperature Sensor: DHT11 Humidity and Temperature Sensor
