# Fritzing sketch MaquinaLav (saved by Fritzing 0.8.5b)
breadboards: 1

parts:
  Componente1 = Arduino Nano (Rev3.0) (ICSP)
  S1 = Pushbutton [package="[THT]"]
  S2 = Pushbutton [package="[THT]"]
  U1 = POT [package=pot_alpha_rv16af-20]
  R1 = Resistor [tolerance=±5% resistance=220 package=THT]
  R2 = Resistor [tolerance=±5% resistance=220 package=THT]

nets:
  N1: Componente1.GND, U1.E, R1.Pin_1, R2.Pin_0
  N2: Componente1.D11/MOSI, S2.Pin_1, S2.Pin_2, R2.Pin_1
  N3: Componente1.D12/MISO, S1.Pin_1, S1.Pin_2, R1.Pin_0
  N4: Componente1.5V, S1.Pin_3, S1.Pin_4, S2.Pin_3, S2.Pin_4, U1.A
  N5: Componente1.A0, U1.S
